// Logisim project project.circ as structural Verilog: 5 circuits, main circuit main
module main (
  output [31:0] INSTRUCTION,
  output [7:0] out_2
);

  wire clock_1_out, RESET_out, uc_1_regw;
  wire [2:0] bit_extender_1_out, bit_extender_2_out, RegEnable, uc_1_x;
  wire [31:0] bancoderegistradores_1_rd1, bancoderegistradores_1_rd2, ula_1_out_4;

  Clock clock_1 (.out(clock_1_out));
  Button RESET (.out(RESET_out));
  ROM #(.dataWidth(32)) rom_1 (.addr(out_2), .data(INSTRUCTION));
  PC pc_1 (.clk(clock_1_out), .reset(RESET_out), .out_3(out_2));
  UC uc_1 (
    .a(INSTRUCTION[28]), .b(INSTRUCTION[29]), .c(INSTRUCTION[30]), .d(INSTRUCTION[31]), .x(uc_1_x[0]),
    .y(uc_1_x[1]), .z(uc_1_x[2]), .regw(uc_1_regw));
  Bit_Extender #(.in_width(4), .out_width(3)) bit_extender_1 (.in(INSTRUCTION[19:16]), .out(bit_extender_1_out));
  Bit_Extender #(.in_width(4), .out_width(3)) bit_extender_2 (.in(INSTRUCTION[23:20]), .out(bit_extender_2_out));
  Bit_Extender #(.in_width(4), .out_width(3)) bit_extender_3 (.in(INSTRUCTION[27:24]), .out(RegEnable));
  BancoDeRegistradores bancoderegistradores_1 (
    .READ1(bit_extender_1_out), .READ2(bit_extender_2_out), .clear(RESET_out), .clk(clock_1_out),
    .Data(ula_1_out_4), .REGEnable(RegEnable), .WriteEnable(uc_1_regw), .RD1(bancoderegistradores_1_rd1),
    .RD2(bancoderegistradores_1_rd2));
  ULA ula_1 (.D1(bancoderegistradores_1_rd1), .D2(bancoderegistradores_1_rd2), .in_3(RegEnable), .out_4(ula_1_out_4));
  RAM #(.dataWidth(32)) ram_1 (.clk(clock_1_out), .din(ula_1_out_4));  // open: addr, we, oe, dout

  // Notes on the sheet:
  //   contents of rom_1 (hex, n*v repeats v):
  //   10001 10001 10001
endmodule

module ULA (
  input  [31:0] D1,
  input  [31:0] D2,
  input  [2:0] in_3,
  output [31:0] out_4
);

  wire [31:0] adder_1_out, negator_1_out, shifter_1_out;

  Adder #(.width(32)) adder_1 (.a(D1), .b(D2), .out(adder_1_out));  // open: cin, cout
  Shifter #(.width(32)) shifter_1 (.in(D1), .\dist (5'b00010), .out(shifter_1_out));
  Multiplier #(.width(32)) multiplier_1 (.a(D1), .b(D2), .out(shifter_1_out));  // open: cin, cout
  Negator #(.width(32)) negator_1 (.in(D1), .out(negator_1_out));
  Multiplexer #(.select(3), .width(32)) multiplexer_1 (
    .in0(adder_1_out), .in1(shifter_1_out), .in2(shifter_1_out), .in3(D1), .in7(negator_1_out), .out(out_4),
    .sel(in_3));  // open: in4, in5, in6
endmodule

module PC (
  input  clk,
  input  reset,
  output [7:0] out_3
);

  wire [31:0] adder_1_out, register_1_q;

  Adder #(.width(32)) adder_1 (
    .a(32'h4), .b({register_1_q[31:10], out_3, register_1_q[1:0]}), .out(adder_1_out));  // open: cin, cout
  Register #(.width(32)) register_1 (
    .D(adder_1_out), .clk(clk), .Q({register_1_q[31:10], out_3, register_1_q[1:0]}), .clr(reset));  // open: en
endmodule

// MUXREG1
module BancoDeRegistradores (
  input  [2:0] READ1,
  input  [2:0] READ2,
  input  clear,
  input  clk,
  input  [31:0] Data,
  input  [2:0] REGEnable,
  input  WriteEnable,
  output [31:0] RD1,
  output [31:0] RD2
);

  wire enaREG0, enaREG1, enaREG2, enaREG3, enaREG4, enaREG5, enaREG6, enaREG7;
  wire [31:0] demultiplexer_1_out0, demultiplexer_1_out1, demultiplexer_1_out2, demultiplexer_1_out3,
       demultiplexer_1_out4, demultiplexer_1_out5, demultiplexer_1_out6, demultiplexer_1_out7, MUXREG0,
       MUXREG1, MUXREG2, MUXREG3, MUXREG4, MUXREG5, MUXREG6, MUXREG7;

  Multiplexer #(.select(3), .width(32)) multiplexer_1 (
    .in0(MUXREG0), .in1(MUXREG1), .in2(MUXREG2), .in3(MUXREG3), .in4(MUXREG4), .in5(MUXREG5), .in6(MUXREG6),
    .in7(MUXREG7), .out(RD1), .sel(READ1));
  Multiplexer #(.select(3), .width(32)) multiplexer_2 (
    .in0(MUXREG0), .in1(MUXREG1), .in2(MUXREG2), .in3(MUXREG3), .in4(MUXREG4), .in5(MUXREG5), .in6(MUXREG6),
    .in7(MUXREG7), .out(RD2), .sel(READ2));
  Demultiplexer #(.select(3), .width(32)) demultiplexer_1 (
    .out0(demultiplexer_1_out0), .out1(demultiplexer_1_out1), .out2(demultiplexer_1_out2),
    .out3(demultiplexer_1_out3), .out4(demultiplexer_1_out4), .out5(demultiplexer_1_out5),
    .out6(demultiplexer_1_out6), .out7(demultiplexer_1_out7), .in(Data), .sel(REGEnable));
  Demultiplexer #(.select(3)) demultiplexer_2 (
    .out0(enaREG0), .out1(enaREG1), .out2(enaREG2), .out3(enaREG3), .out4(enaREG4), .out5(enaREG5),
    .out6(enaREG6), .out7(enaREG7), .in(WriteEnable), .sel(REGEnable));
  Register #(.width(32)) REG0 (.D(demultiplexer_1_out0), .en(enaREG0), .clk(clk), .Q(MUXREG0), .clr(clear));
  Register #(.width(32)) REG1 (.D(demultiplexer_1_out1), .en(enaREG1), .clk(clk), .Q(MUXREG1), .clr(clear));
  Register #(.width(32)) REG2 (.D(demultiplexer_1_out2), .en(enaREG2), .clk(clk), .Q(MUXREG2), .clr(clear));
  Register #(.width(32)) REG3 (.D(demultiplexer_1_out3), .en(enaREG3), .clk(clk), .Q(MUXREG3), .clr(clear));
  Register #(.width(32)) REG4 (.D(demultiplexer_1_out4), .en(enaREG4), .clk(clk), .Q(MUXREG4), .clr(clear));
  Register #(.width(32)) REG5 (.D(demultiplexer_1_out5), .en(enaREG5), .clk(clk), .Q(MUXREG5), .clr(clear));
  Register #(.width(32)) REG6 (.D(demultiplexer_1_out6), .en(enaREG6), .clk(clk), .Q(MUXREG6), .clr(clear));
  Register #(.width(32)) REG7 (.D(demultiplexer_1_out7), .en(enaREG7), .clk(clk), .Q(MUXREG7));  // open: clr
endmodule

module UC (
  input  a,
  input  b,
  input  c,
  input  d,
  output x,
  output y,
  output z,
  output regw
);

  wire and_1_out, and_2_out, and_3_out, and_4_out, and_5_out, and_6_out, and_7_out, and_8_out, and_9_out,
       and_10_out, not_1_out, not_2_out, not_3_out;

  not not_1 (not_1_out, b);
  not not_2 (not_2_out, c);
  not not_3 (not_3_out, d);
  and and_1 (and_1_out, b, not_2_out);
  and and_2 (and_2_out, b, not_3_out);
  and and_3 (and_3_out, not_1_out, c);
  and and_4 (and_4_out, c, not_3_out);
  and and_5 (and_5_out, not_1_out, d);
  and and_6 (and_6_out, not_2_out, d);
  and and_7 (and_7_out, not_1_out, d);
  and and_8 (and_8_out, not_1_out, c);
  and and_9 (and_9_out, b, not_2_out);
  and and_10 (and_10_out, c, not_3_out);
  or or_1 (x, and_1_out, and_2_out);
  or or_2 (y, and_3_out, and_4_out);
  or or_3 (z, and_5_out, and_6_out);
  or or_4 (regw, and_7_out, and_8_out, and_9_out, and_10_out);
endmodule
